# Fritzing sketch measure_capacity_schematic (saved by Fritzing 0.9.3b)
breadboards: 1

parts:
  IC1 = MICROCONTROLLER [package=dil28-3-zif_socket]
  C1 = Capacitor [package=cap-pth-small2]
  R1 = Resistor [tolerance=±5% resistance=4.7k package=THT]
  R2 = Resistor [tolerance=±5% resistance=4.7k package=THT]
  LED1 = LED - 5mm [color="Green (565nm)" package="5 mm [THT]"]
  R3 = Resistor [tolerance=±5% resistance=2.2k package=THT]
  Raspberry_Pi_1 = Raspberry Pi 2
  Maluska1 = maluska dil miniaturrelais [part_number="DIL Mini RY" package=THT]
  D1 = Rectifier Diode [part_number=1N4001 package="300 mil [THT]"]
  R4 = Resistor [tolerance=±5% resistance=5 package=THT]
  Q1 = MOSFET-NCHANNEL [package=to-92]
  LED2 = LED - 5mm [color="Red (633nm)" package="5 mm [THT]"]
  R5 = Resistor [tolerance=±5% resistance=1k package=THT]
  R6 = Resistor [tolerance=±5% resistance=1 package=THT]
  R7 = Resistor [tolerance=±5% resistance=1 package=THT]
  U2 = Battery Holders [package=battery-aa]

nets:
  3V3: IC1.VCC, IC1.AVCC, R1.Pin_0, R2.Pin_0, Raspberry_Pi_1.3v3, Raspberry_Pi_1.3V3
  GND: IC1.GND, C1.2, R3.Pin_1, Raspberry_Pi_1.GND, Q1.S, LED2.cathode, R7.Pin_1, U2.-
  N1: IC1.PB0(ICP), LED1.anode
  N2: IC1.AREF, C1.1
  N3: IC1.PC0(ADC0), R6.Pin_1, R7.Pin_0
  N4: IC1.PC4(ADC4_SDA), R2.Pin_1, Raspberry_Pi_1.GPIO2
  N5: IC1.PC5(ADC5_SCL), R1.Pin_1, Raspberry_Pi_1.GPIO3
  N6: LED1.cathode, R3.Pin_0
  N7: Raspberry_Pi_1.GPIO21, Q1.G, R5.Pin_0
  N8: Raspberry_Pi_1.5V, Maluska1.1, D1.cathode
  N9: Maluska1.4, U2.+
  N10: Maluska1.8, R6.Pin_0
  N11: Maluska1.16, D1.anode, R4.Pin_0
  N12: R4.Pin_1, Q1.D
  N13: LED2.anode, R5.Pin_1
